// Logisim project Circuit.circ as structural Verilog: 3 circuits, main circuit main
// FSM
module main (
  input  enter___clk,
  input  reset,
  input  inb0,
  input  inb1,
  input  inb2,
  output Fail,
  output Open
);

  wire AnyFail_out, FAIL_q, FAIL_qn, FCLK_out, not_1_out, not_2_out, not_3_out, not_4_out, not_5_out,
       not_6_out, not_7_out, not_8_out, not_9_out, not_10_out, not_11_out, not_12_out, not_13_out,
       not_14_out, not_15_out, not_16_out, not_17_out, not_18_out, S0_out, S0F_out, S0R_out, S1_out,
       S01F_out, S1F_out, S2_out, S2F_out, S3_out, S3F_out, S4_out, S4F_out, S5_out, S12F_out, S23F_out,
       S34F_out, S45F_out;
  wire [2:0] ripple_mod_5_1_out;

  not not_1 (not_1_out, ripple_mod_5_1_out[1]);
  not not_2 (not_2_out, inb0);
  not not_3 (not_3_out, ripple_mod_5_1_out[0]);
  not not_4 (not_4_out, inb0);
  not not_5 (not_5_out, ripple_mod_5_1_out[2]);
  not not_6 (not_6_out, ripple_mod_5_1_out[0]);
  not not_7 (not_7_out, ripple_mod_5_1_out[2]);
  not not_8 (not_8_out, inb0);
  not not_9 (not_9_out, ripple_mod_5_1_out[2]);
  not not_10 (not_10_out, inb1);
  not not_11 (not_11_out, ripple_mod_5_1_out[0]);
  not not_12 (not_12_out, ripple_mod_5_1_out[2]);
  and S5 (S5_out, ripple_mod_5_1_out[0], not_1_out, ripple_mod_5_1_out[2]);
  nand S4F (S4F_out, not_2_out, inb1, inb2);
  not not_13 (not_13_out, ripple_mod_5_1_out[1]);
  and S4 (S4_out, not_3_out, not_13_out, ripple_mod_5_1_out[2]);
  nand S3F (S3F_out, not_4_out, inb1, inb2);
  and S3 (S3_out, ripple_mod_5_1_out[0], ripple_mod_5_1_out[1], not_5_out);
  nand S2F (S2F_out, inb0, inb1, not_14_out);
  not not_14 (not_14_out, inb2);
  and S2 (S2_out, not_6_out, ripple_mod_5_1_out[1], not_7_out);
  nand S1F (S1F_out, not_8_out, not_15_out, inb2);
  not not_15 (not_15_out, inb1);
  not not_16 (not_16_out, ripple_mod_5_1_out[1]);
  and S1 (S1_out, ripple_mod_5_1_out[0], not_16_out, not_9_out);
  nand S0F (S0F_out, inb0, not_10_out, inb2);
  not not_17 (not_17_out, ripple_mod_5_1_out[1]);
  and S0 (S0_out, not_11_out, not_17_out, not_12_out);
  // Probe on ripple_mod_5_1_out
  ripple_mod_5 ripple_mod_5_1 (.CLK(enter___clk), .RESET(reset), .OUT(ripple_mod_5_1_out));
  // Probe on {inb2, inb1, inb0}
  and S45F (S45F_out, S5_out, S4F_out);
  and S34F (S34F_out, S4_out, S3F_out);
  and S23F (S23F_out, S3_out, S2F_out);
  and S12F (S12F_out, S2_out, S1F_out);
  and S01F (S01F_out, S1_out, S0F_out);
  not not_18 (not_18_out, enter___clk);
  or AnyFail (AnyFail_out, S45F_out, S34F_out, S23F_out, S12F_out, S01F_out);
  and S0R (S0R_out, S0_out, not_18_out);
  and FCLK (FCLK_out, AnyFail_out, enter___clk, FAIL_qn);
  D_Flip_Flop #(.trigger("falling")) u_FAIL (
    .clk(FCLK_out), .D(AnyFail_out), .Q(FAIL_q), .Qn(FAIL_qn), .reset(S0R_out));  // open: preset, en
  and Fout (Fail, S5_out, FAIL_q);
  and Oout (Open, S5_out, FAIL_qn, not_18_out);
endmodule

// 5M
module ripple_mod_5 (
  input  CLK,
  input  RESET,
  output [2:0] OUT
);

  wire and_1_out, not_1_out, or_1_out, Sb0_qn, Sb1_qn;

  or or_1 (or_1_out, RESET, and_1_out);
  and and_1 (and_1_out, not_1_out, OUT[1], OUT[2]);
  T_Flip_Flop Sb0 (.clk(CLK), .T(1'b1), .Q(OUT[0]), .Qn(Sb0_qn), .reset(or_1_out));  // open: preset, en
  T_Flip_Flop Sb1 (.clk(Sb0_qn), .T(1'b1), .Q(OUT[1]), .Qn(Sb1_qn), .reset(or_1_out));  // open: preset, en
  T_Flip_Flop Sb2 (.clk(Sb1_qn), .T(1'b1), .Q(OUT[2]), .reset(or_1_out));  // open: Qn, preset, en
  not not_1 (not_1_out, OUT[0]);
endmodule

module outside (
  input  enter___clk,
  input  reset,
  input  inb0,
  input  inb1,
  input  inb2
);

  wire main_1_fail, main_1_open;

  main main_1 (
    .enter___clk(enter___clk), .reset(reset), .inb0(inb0), .inb1(inb1), .inb2(inb2), .Fail(main_1_fail),
    .Open(main_1_open));
  // Probe on main_1_fail
  // Probe on main_1_open
endmodule
